// Logisim project HERA Processor.circ as structural Verilog: 17 circuits, main circuit main
module Instruction_Memory (
  input  Clock,
  output [15:0] out_2
);

  wire [15:0] PC_q;

  Counter #(.width(16), .max('hffff), .ongoal("stay")) PC (.Q(PC_q), .clk(Clock));  // open: load, D, count, carry, clr
  ROM #(.addrWidth(16), .dataWidth(16)) rom_1 (.addr(PC_q), .data(out_2));  // open: sel

  // Notes on the sheet:
  //   I don't feel like using this in my main much. I want to see the ROM out there instead of having only a 16 bit representation of the hera instructions as output
  //   contents of rom_1 (hex, n*v repeats v):
  //   3165 3170 3965 3178
endmodule

module Register_Bank (
  input  [3:0] a,
  input  [3:0] d,
  input  [3:0] b,
  input  Call_return,
  input  Clock,
  input  [15:0] Rd,
  output [15:0] R1,
  output [15:0] R2,
  output [15:0] R3,
  output [15:0] Ra,
  output [15:0] Rb,
  output [15:0] Rd_2
);

  wire a1, a2, a3, a4, a5, a6, a7, a8, a9, a10, a11, a12, a13, a14, a15, and_1_out, and_2_out, and_3_out,
       and_4_out, and_5_out, and_6_out, and_7_out, and_8_out, and_9_out, and_10_out, and_11_out, and_12_out,
       and_13_out, and_14_out, and_15_out, d1, d2, d3, d4, d5, d6, d7, d8, d9, d10, d11, d12, d13, d14, d15,
       decoder_1_out0, or_1_out, or_2_out, or_3_out, or_4_out, or_5_out, or_6_out, or_7_out, or_8_out,
       or_9_out, or_10_out, or_11_out, or_12_out, or_13_out, or_14_out, or_15_out;
  wire [15:0] multiplexer_2_out, multiplexer_3_out, multiplexer_4_out, multiplexer_5_out, multiplexer_6_out,
       multiplexer_7_out, multiplexer_8_out, multiplexer_9_out, multiplexer_10_out, multiplexer_11_out,
       multiplexer_12_out, multiplexer_13_out, multiplexer_14_out, multiplexer_15_out, R0_q, R4_q, R5_q,
       R6_q, R7_q, R8_q, R9_q, R10_q, R11_q, R12_q, R13_q, R14, R15_q, Ra_or_Rd;

  Decoder #(.select(4)) decoder_1 (
    .out0(decoder_1_out0), .out1(d1), .out2(d2), .out3(d3), .out4(d4), .out5(d5), .out6(d6), .out7(d7),
    .out8(d8), .out9(d9), .out10(d10), .out11(d11), .out12(d12), .out13(d13), .out14(d14), .out15(d15),
    .sel(d));  // open: en
  Decoder #(.select(4)) decoder_2 (
    .out1(a1), .out2(a2), .out3(a3), .out4(a4), .out5(a5), .out6(a6), .out7(a7), .out8(a8), .out9(a9),
    .out10(a10), .out11(a11), .out12(a12), .out13(a13), .out14(a14), .out15(a15), .sel(a));  // open: out0, en
  and and_1 (and_1_out, Call_return, a1);
  and and_2 (and_2_out, Call_return, a2);
  and and_3 (and_3_out, Call_return, a3);
  and and_4 (and_4_out, Call_return, a14);
  Multiplexer #(.width(16)) multiplexer_1 (.in0(Rd), .in1(Ra), .out(Ra_or_Rd), .sel(Call_return));  // open: en
  or or_1 (or_1_out, d1, and_1_out);
  Multiplexer #(.width(16)) multiplexer_2 (.in0(R14), .in1(Rd), .out(multiplexer_2_out), .sel(d2));  // open: en
  or or_2 (or_2_out, d2, and_2_out);
  or or_3 (or_3_out, d3, and_3_out);
  Multiplexer #(.width(16)) multiplexer_3 (.in0(R14), .in1(Rd), .out(multiplexer_3_out), .sel(d4));  // open: en
  or or_4 (or_4_out, d4, and_5_out);
  and and_5 (and_5_out, Call_return, a4);
  Multiplexer #(.width(16)) multiplexer_4 (.in0(R14), .in1(Rd), .out(multiplexer_4_out), .sel(d5));  // open: en
  and and_6 (and_6_out, Call_return, a5);
  Multiplexer #(.width(16)) multiplexer_5 (.in0(R14), .in1(Rd), .out(multiplexer_5_out), .sel(d6));  // open: en
  and and_7 (and_7_out, Call_return, a6);
  and and_8 (and_8_out, Call_return, a8);
  Multiplexer #(.width(16)) multiplexer_6 (.in0(R14), .in1(Rd), .out(multiplexer_6_out), .sel(d10));  // open: en
  and and_9 (and_9_out, Call_return, a10);
  and and_10 (and_10_out, Call_return, a11);
  and and_11 (and_11_out, Call_return, a12);
  Multiplexer #(.width(16)) multiplexer_7 (.in0(R14), .in1(Rd), .out(multiplexer_7_out), .sel(d13));  // open: en
  or or_5 (or_5_out, d14, and_4_out);
  Register #(.width(16)) R0 (.D({16{1'b0}}), .en(decoder_1_out0), .Q(R0_q), .clk(Clock));  // open: clr
  Multiplexer #(.width(16)) multiplexer_8 (.in0(R14), .in1(Rd), .out(multiplexer_8_out), .sel(d1));  // open: en
  Register #(.width(16)) u_R1 (.D(multiplexer_8_out), .en(or_1_out), .Q(R1), .clk(Clock));  // open: clr
  Register #(.width(16)) u_R2 (.D(multiplexer_2_out), .en(or_2_out), .Q(R2), .clk(Clock));  // open: clr
  Multiplexer #(.width(16)) multiplexer_9 (.in0(R14), .in1(Rd), .out(multiplexer_9_out), .sel(d3));  // open: en
  Register #(.width(16)) u_R3 (.D(multiplexer_9_out), .en(or_3_out), .Q(R3), .clk(Clock));  // open: clr
  Register #(.width(16)) R4 (.D(multiplexer_3_out), .en(or_4_out), .Q(R4_q), .clk(Clock));  // open: clr
  Register #(.width(16)) R5 (.D(multiplexer_4_out), .en(or_6_out), .Q(R5_q), .clk(Clock));  // open: clr
  or or_6 (or_6_out, d5, and_6_out);
  Register #(.width(16)) R6 (.D(multiplexer_5_out), .en(or_7_out), .Q(R6_q), .clk(Clock));  // open: clr
  or or_7 (or_7_out, d6, and_7_out);
  and and_12 (and_12_out, Call_return, a7);
  Multiplexer #(.width(16)) multiplexer_10 (.in0(R14), .in1(Rd), .out(multiplexer_10_out), .sel(d8));  // open: en
  Register #(.width(16)) R8 (.D(multiplexer_10_out), .en(or_8_out), .Q(R8_q), .clk(Clock));  // open: clr
  or or_8 (or_8_out, d8, and_8_out);
  and and_13 (and_13_out, Call_return, a9);
  or or_9 (or_9_out, d10, and_9_out);
  Multiplexer #(.width(16)) multiplexer_11 (.in0(R14), .in1(Rd), .out(multiplexer_11_out), .sel(d11));  // open: en
  Multiplexer #(.width(16)) multiplexer_12 (.in0(R14), .in1(Rd), .out(multiplexer_12_out), .sel(d12));  // open: en
  or or_10 (or_10_out, d12, and_11_out);
  Register #(.width(16)) u_R14 (.D(Ra_or_Rd), .en(or_5_out), .Q(R14), .clk(Clock));  // open: clr
  Multiplexer #(.width(16)) multiplexer_13 (.in0(R14), .in1(Rd), .out(multiplexer_13_out), .sel(d15));  // open: en
  Multiplexer #(.width(16)) multiplexer_14 (.in0(R14), .in1(Rd), .out(multiplexer_14_out));  // open: sel, en
  or or_11 (or_11_out, d7, and_12_out);
  Multiplexer #(.width(16)) multiplexer_15 (.in0(R14), .in1(Rd), .out(multiplexer_15_out), .sel(d9));  // open: en
  or or_12 (or_12_out, d11, and_10_out);
  Register #(.width(16)) R12 (.D(multiplexer_12_out), .en(or_10_out), .Q(R12_q), .clk(Clock));  // open: clr
  and and_14 (and_14_out, Call_return, a13);
  and and_15 (and_15_out, Call_return, a15);
  Register #(.width(16)) R7 (.D(multiplexer_14_out), .en(or_11_out), .Q(R7_q), .clk(Clock));  // open: clr
  Register #(.width(16)) R9 (.D(multiplexer_15_out), .en(or_13_out), .Q(R9_q), .clk(Clock));  // open: clr
  or or_13 (or_13_out, d9, and_13_out);
  Register #(.width(16)) R10 (.D(multiplexer_6_out), .en(or_9_out), .Q(R10_q), .clk(Clock));  // open: clr
  Register #(.width(16)) R11 (.D(multiplexer_11_out), .en(or_12_out), .Q(R11_q), .clk(Clock));  // open: clr
  Register #(.width(16)) R13 (.D(multiplexer_7_out), .en(or_14_out), .Q(R13_q), .clk(Clock));  // open: clr
  or or_14 (or_14_out, d13, and_14_out);
  Register #(.width(16)) R15 (.D(multiplexer_13_out), .en(or_15_out), .Q(R15_q), .clk(Clock));  // open: clr
  or or_15 (or_15_out, d15, and_15_out);
  Multiplexer #(.select(4), .width(16)) multiplexer_16 (
    .in0(R0_q), .in1(R1), .in2(R2), .in3(R3), .in4(R4_q), .in5(R5_q), .in6(R6_q), .in7(R7_q), .in8(R8_q),
    .in9(R9_q), .in10(R10_q), .in11(R11_q), .in12(R12_q), .in13(R13_q), .in14(R14), .in15(R15_q), .out(Ra),
    .sel(a));  // open: en
  Multiplexer #(.select(4), .width(16)) multiplexer_17 (
    .in0(R0_q), .in1(R1), .in2(R2), .in3(R3), .in4(R4_q), .in5(R5_q), .in6(R6_q), .in7(R7_q), .in8(R8_q),
    .in9(R9_q), .in10(R10_q), .in11(R11_q), .in12(R12_q), .in13(R13_q), .in14(R14), .in15(R15_q), .out(Rb),
    .sel(b));  // open: en
  Multiplexer #(.select(4), .width(16)) multiplexer_18 (
    .in0(R0_q), .in1(R1), .in2(R2), .in3(R3), .in4(R4_q), .in5(R5_q), .in6(R6_q), .in7(R7_q), .in8(R8_q),
    .in9(R9_q), .in10(R10_q), .in11(R11_q), .in12(R12_q), .in13(R13_q), .in14(R14), .in15(R15_q), .out(Rd_2),
    .sel(d));  // open: en

  // Other names for the same wires on the sheet: c_r = Call_return

  // Notes on the sheet:
  //   if it is, Rd goes into the register
  //   else, R14 goes into the register
  //   this will actually be b if call/return
  //   write R14 to Ra if call/return
  //   16 mux are to decide if register is chosen by d
  //   OR gates are to enable register changing when chosen either by d or a
  //   Decide what goes into R14
endmodule

module Flag_Bank (
  input  [4:0] Flags,
  input  Clk,
  output [4:0] Flags_Out
);

  Register #(.width(1)) F0__Sign (.D(Flags[0]), .Q(Flags_Out[0]), .clk(Clk));  // open: en, clr
  Register #(.width(1)) F1__Zero (.D(Flags[1]), .Q(Flags_Out[1]), .clk(Clk));  // open: en, clr
  Register #(.width(1)) F2__Overflow (.D(Flags[2]), .Q(Flags_Out[2]), .clk(Clk));  // open: en, clr
  Register #(.width(1)) F3__Carry (.D(Flags[3]), .Q(Flags_Out[3]), .clk(Clk));  // open: en, clr
  Register #(.width(1)) F4__Carry_block (.D(Flags[4]), .Q(Flags_Out[4]), .clk(Clk));  // open: en, clr

  // Notes on the sheet:
  //   This module don't do much. I just want my flags to be clocked.
endmodule

module Shifts (
  input  [4:0] Flags,
  input  [3:0] a,
  input  [15:0] Rb,
  output [15:0] Rd,
  output [4:0] Flags_2
);

  wire add_d_b_b_1_overflow;
  wire [15:0] bit_extender_1_out, or_1_out, or_2_out, shifter_1_out, shifter_2_out, shifter_3_out;
  wire [15:15] and_1_out;

  and and_1 (and_1_out[15], Flags[3], ~Flags[4]);  // AND_Gate
  assign bit_extender_1_out = {{15{1'b0}}, and_1_out[15]};  // Bit_Extender bit_extender_1
  Shifter #(.width(16)) shifter_1 (.in(Rb), .\dist (4'b0001), .out(shifter_1_out));
  Shifter #(.width(16), .shift("lr")) shifter_2 (.in(Rb), .\dist (4'b0001), .out(shifter_2_out));
  Shifter #(.width(16), .shift("ar")) shifter_3 (.in(Rb), .\dist (4'b0001), .out(shifter_3_out));
  assign or_1_out = shifter_1_out | bit_extender_1_out;  // OR_Gate or_1, 16 bits wide
  assign or_2_out = shifter_2_out | {and_1_out[15], {15{1'b0}}};  // OR_Gate or_2, 16 bits wide
  ADD_d_b_b add_d_b_b_1 (.Rb(Rb), .overflow(add_d_b_b_1_overflow));
  Multiplexer #(.select(3), .width(16)) multiplexer_1 (
    .in0(or_1_out), .in1(or_2_out), .in2(Rb), .in3(Rb), .in4(or_1_out), .in5(shifter_3_out), .in6(Rb),
    .in7(Rb), .out({Flags_2[0], Rd[14:0]}), .sel(a[2:0]));  // open: en
  Multiplexer #(.select(3)) multiplexer_2 (
    .in0(Rb[15]), .in1(Rb[0]), .in2(Flags[3]), .in3(Flags[3]), .in4(Rb[15]), .in5(Rb[0]), .in6(Flags[3]),
    .in7(Flags[3]), .out(Flags_2[3]), .sel(a[2:0]));  // open: en
  Multiplexer #(.select(3)) multiplexer_3 (
    .in0(Flags[2]), .in1(Flags[2]), .in2(Flags[2]), .in3(Flags[2]), .in4(add_d_b_b_1_overflow),
    .in5(Flags[2]), .in6(Flags[2]), .in7(Flags[2]), .out(Flags_2[2]), .sel(a[2:0]));  // open: en
  Comparator #(.width(16)) comparator_1 (.a({Flags_2[0], Rd[14:0]}), .b({16{1'b0}}), .eq(Flags_2[1]));  // open: gt, lt

  assign Flags_2[4] = Flags[4];
  assign Rd[15] = Flags_2[0];

  // Other names for the same wires on the sheet: a2a1a0[2:0] = a[2:0]

  // Notes on the sheet:
  //   Flags: pull=up
  //   LSR and ASR are basically the same, except for ASL doesnt shift in the carry
  //   LSL and ASL are also the same, except for ASL changes overflow
  //   ASR
  //   LSL + ASL
  //   LSR
  //   Check which kind of shift
endmodule

module FON__FOFF__FSET (
  input  [3:0] b,
  input  [4:0] Flags_in,
  input  [3:0] d,
  output [4:0] Flags
);

  wire [4:0] FOFF, FON;

  or or_1 (FON[0], b[0], Flags_in[0]);
  and and_1 (FOFF[0], ~b[0], Flags_in[0]);  // AND_Gate
  or or_2 (FON[1], b[1], Flags_in[1]);
  and and_2 (FOFF[1], ~b[1], Flags_in[1]);  // AND_Gate
  or or_3 (FON[2], b[2], Flags_in[2]);
  and and_3 (FOFF[2], ~b[2], Flags_in[2]);  // AND_Gate
  or or_4 (FON[3], b[3], Flags_in[3]);
  and and_4 (FOFF[3], ~b[3], Flags_in[3]);  // AND_Gate
  or or_5 (FON[4], Flags_in[4], d[0]);
  and and_5 (FOFF[4], ~d[0], Flags_in[4]);  // AND_Gate
  Multiplexer #(.select(3), .width(5)) multiplexer_1 (
    .in0(FON), .in1({d[0], Flags_in[4], Flags_in[2:0]}), .in2({d[0], b}),
    .in3({d[0], Flags_in[4], Flags_in[2:0]}), .in4(FOFF), .in5({d[0], Flags_in[4], Flags_in[2:0]}),
    .in6({Flags_in[4], b}), .in7({d[0], Flags_in[4], Flags_in[2:0]}), .out(Flags), .sel(d[3:1]));  // open: en

  // Other names for the same wires on the sheet: d3d2d1[2:0] = d[3:1]; FSET4[4:0] = {d[0], b};
  //   FSET5[4:0] = {Flags_in[4], b}

  // Notes on the sheet:
  //   Flags_in: pull=up
  //   This module is tested. It seems to work properly ^
endmodule

module SAVEF__RSTRF (
  input  [4:0] Flags,
  input  [15:0] Rd,
  input  bit_3,
  output [4:0] Flags_2,
  output [15:0] Rd_2
);

  Multiplexer #(.width(5)) multiplexer_1 (.in0(Flags), .in1(Rd[4:0]), .out(Flags_2), .sel(bit_3));  // open: en
  Multiplexer #(.width(16)) multiplexer_2 (.in0({{11{1'b0}}, Flags}), .in1(Rd), .out(Rd_2), .sel(bit_3));  // open: en

  // Notes on the sheet:
  //   Flags: pull=up
  //   SAVEF: Extend flag to 16 bits and assign that to Rd, flags not affected
  //   RSTRF: Rd not affected, assign 5 least significant bits of Rd to flags
  //   The two multiplexer is to check whether its SAVEF or RSTRF. Select line is bit 3 which is the most significant bit of a
  //   This module is used to handle changes to Flags and Rd made by SAVEF/RSTRF. It was tested
endmodule

module Flags__AND__OR__XOR__LOAD (
  input  [4:0] Flags,
  input  [15:0] Rd_out,
  output [4:0] Flags_2
);

  Comparator #(.width(16)) comparator_1 (.a(Rd_out), .b({16{1'b0}}), .eq(Flags_2[1]));  // open: gt, lt

  assign {Flags_2[4:2], Flags_2[0]} = {Flags[4:2], Rd_out[15]};

  // Notes on the sheet:
  //   Only Sign and Zero are affected by these operations
  //   These flags are decided by the final outcome Rd
endmodule

module Flags__ADD__SUB (
  input  [4:0] Flags,
  input  [15:0] Rd_out,
  input  Carry_Out,
  input  Borrow_out,
  input  [15:0] Ra,
  input  [15:0] Rb,
  input  [3:0] Opcode,
  output [4:0] Flags_2
);

  wire and_1_out, and_2_out, and_3_out, and_4_out, not_1_out, or_1_out, or_2_out;

  Comparator #(.width(16)) comparator_1 (.a(Rd_out), .b({16{1'b0}}), .eq(Flags_2[1]));  // open: gt, lt
  and and_1 (and_1_out, Rd_out[15], ~Ra[15], ~Rb[15]);  // AND_Gate
  and and_2 (and_2_out, ~Rd_out[15], Ra[15], Rb[15]);  // AND_Gate
  and and_3 (and_3_out, Rd_out[15], ~Ra[15], Rb[15]);  // AND_Gate
  and and_4 (and_4_out, ~Rd_out[15], Ra[15], ~Rb[15]);  // AND_Gate
  or or_1 (or_1_out, and_1_out, and_2_out);
  or or_2 (or_2_out, and_3_out, and_4_out);
  Multiplexer multiplexer_1 (.in0(or_1_out), .in1(or_2_out), .out(Flags_2[2]), .sel(Opcode[0]));  // open: en
  not not_1 (not_1_out, Borrow_out);
  Multiplexer multiplexer_2 (.in0(Carry_Out), .in1(not_1_out), .out(Flags_2[3]), .sel(Opcode[0]));  // open: en

  assign {Flags_2[4], Flags_2[0]} = {Flags[4], Rd_out[15]};

  // Notes on the sheet:
  //   ADD/SUB affects carry, zero, sign, overflow
  //   Sign
  //   Check if op is sub/add
  //   Carry Block
  //   Zero
endmodule

module Flags__All_with_code_3 (
  input  [15:0] Rd_in,
  input  [15:0] Rb_in,
  input  [4:0] Flags,
  input  [3:0] a,
  input  [3:0] b,
  input  [3:0] d,
  output [4:0] out_7
);

  wire [4:0] FON_FOFF_flags, multiplexer_1_out, SAVE_RESTORE_flags_2, Shift_flags_2;

  Shifts Shift (.Flags(Flags), .Rb(Rb_in), .a(a), .Flags_2(Shift_flags_2));  // open: Rd
  SAVEF__RSTRF SAVE_RESTORE (.Flags(Flags), .Rd(Rd_in), .bit_3(b[3]), .Flags_2(SAVE_RESTORE_flags_2));  // open: Rd_2
  FON__FOFF__FSET FON_FOFF (.b(b), .Flags_in(Flags), .d(d), .Flags(FON_FOFF_flags));
  Multiplexer #(.width(5)) multiplexer_1 (
    .in0(FON_FOFF_flags), .in1(SAVE_RESTORE_flags_2), .out(multiplexer_1_out), .sel(a[0]));  // open: en
  Multiplexer #(.select(3), .width(5)) multiplexer_2 (
    .in0(Shift_flags_2), .in1(Flags), .in2(Shift_flags_2), .in3(multiplexer_1_out), .in4(Flags), .in5(Flags),
    .in6(Flags), .in7(Flags), .out(out_7), .sel(a[3:1]));  // open: en

  // Other names for the same wires on the sheet: Flags_in[4:0] = Flags

  // Notes on the sheet:
  //   FON, FOFF affects all
  //   LSL, LSR affects sign, zero and carry
  //   Use SAVEF, RSTRF module to get the flags for those. Need Rd and a as input
endmodule

module ALSU (
  input  [4:0] Flags_in,
  input  [15:0] Ra,
  input  [3:0] Opcode,
  input  [15:0] Rb,
  input  [3:0] a,
  input  [3:0] b,
  input  [3:0] d,
  input  [15:0] Rd,
  input  [15:0] Load_Store_Value,
  output [4:0] Flags,
  output [15:0] Rd_2
);

  wire b_in, b_out, c_in, c_out, d_out, i_out, subtractor_2_bout;
  wire [15:0] ADD, adder_2_out, adder_3_out, AND, bit_extender_1_out, bit_extender_2_out, DEC, INC, Mul_out,
       multiplexer_1_out, multiplexer_2_out, OR, Save_Restore_rd_2, SETLO, Shift_p5, SUB, XOR;

  and and_1 (c_in, Flags_in[3], ~Flags_in[4]);  // AND_Gate
  and and_2 (b_in, ~Flags_in[3], ~Flags_in[4]);  // AND_Gate
  assign bit_extender_1_out = {{11{1'b0}}, {a[0], b}};  // Bit_Extender bit_extender_1
  assign bit_extender_2_out = {{11{1'b0}}, {a[0], b}};  // Bit_Extender bit_extender_2
  assign AND = Ra & Rb;  // AND_Gate AND_3, 16 bits wide
  assign OR = Ra | Rb;  // OR_Gate OR, 16 bits wide
  assign XOR = Ra ^ Rb;  // XOR_Gate XOR, 16 bits wide
  Adder #(.width(16)) adder_1 (.a(Ra), .b(Rb), .out(ADD), .cin(c_in), .cout(c_out));
  Subtractor #(.width(16)) subtractor_1 (.a(Ra), .b(Rb), .out(SUB), .bin(b_in), .bout(b_out));
  Adder #(.width(16)) adder_2 (.a(bit_extender_1_out), .b(16'h1), .out(adder_2_out));  // open: cin, cout
  Adder #(.width(16)) adder_3 (.a(bit_extender_2_out), .b(16'h1), .out(adder_3_out));  // open: cin, cout
  assign SETLO = {{8{a[3]}}, {a, b}};  // Bit_Extender bit_extender_3
  Adder #(.width(16)) adder_4 (.a(adder_2_out), .b(Rd), .out(INC), .cout(i_out));  // open: cin
  Subtractor #(.width(16)) subtractor_2 (.a(Rd), .b(adder_3_out), .out(DEC), .bout(subtractor_2_bout));  // open: bin
  not not_1 (d_out, subtractor_2_bout);
  // Shifts Shift: pin names not known; wires that end beside it: Flags_in, Rb, b, a, Shift_p5
  Multiply multiply_1 (.Ra(Ra), .Rb(Rb), .Flags_in(Flags_in), .Rd(Mul_out));  // open: Flags_out
  SAVEF__RSTRF Save_Restore (.Flags(Flags_in), .Rd(Rd), .bit_3(b[3]), .Rd_2(Save_Restore_rd_2));  // open: Flags_2
  Multiplexer #(.width(16)) multiplexer_1 (
    .in0(Rd), .in1(Save_Restore_rd_2), .out(multiplexer_1_out), .sel(a[0]));  // open: en
  Multiplexer #(.select(3), .width(16)) multiplexer_2 (
    .in0(Shift_p5), .in1(Rd), .in2(Shift_p5), .in3(multiplexer_1_out), .in4(INC), .in5(INC), .in6(DEC),
    .in7(DEC), .out(multiplexer_2_out), .sel(a[3:1]));  // open: en
  All_Flags Flags_Module (
    .Borrow_out(b_out), .Carry_out(c_out), .Flags(Flags_in), .Ra(Ra), .Rb(Rb), .Rd_in(Rd), .dec_out(d_out),
    .Rd_out(Rd_2), .inc_out(i_out), .a(a), .b(b), .d(d), .Opcode(Opcode), .Flags_2(Flags));
  Multiplexer #(.select(4), .width(16)) multiplexer_3 (
    .in0(Rd), .in1(Rd), .in2(Rd), .in3(multiplexer_2_out), .in4(Load_Store_Value), .in5(Load_Store_Value),
    .in6(Rd), .in7(Rd), .in8(AND), .in9(OR), .in10(ADD), .in11(SUB), .in12(Mul_out), .in13(XOR),
    .in14(SETLO), .in15({a, b, Rd[7:0]}), .out(Rd_2), .sel(Opcode));  // open: en

  // Other names for the same wires on the sheet: Load_store_val[15:0] = Load_Store_Value; Rd_in[15:0] = Rd;
  //   SETHI[15:0] = {a, b, Rd[7:0]}; Rd_out[15:0] = Rd_2; a3a2a1[2:0] = a[3:1]

  // Notes on the sheet:
  //   Flags_in: pull=up
endmodule

module All_Flags (
  input  Borrow_out,
  input  Carry_out,
  input  [4:0] Flags,
  input  [15:0] Ra,
  input  [15:0] Rb,
  input  [15:0] Rd_in,
  input  dec_out,
  input  [3:0] Opcode,
  input  [15:0] Rd_out,
  input  inc_out,
  input  [3:0] a,
  input  [3:0] b,
  input  [3:0] d,
  output [4:0] Flags_2
);

  wire [4:0] ADD_SUB_flags_2, AND__OR__XOR__LOAD_flags_2, Code_3_out_7, flags_inc_dec_1_flags_2,
       multiplexer_1_out, Multiplier_flags_out;

  Flags__ADD__SUB ADD_SUB (
    .Flags(Flags), .Rd_out(Rd_out), .Carry_Out(Carry_out), .Borrow_out(Borrow_out), .Ra(Ra), .Rb(Rb),
    .Opcode(Opcode), .Flags_2(ADD_SUB_flags_2));
  Flags__All_with_code_3 Code_3 (.Rd_in(Rd_in), .Rb_in(Rb), .Flags(Flags), .a(a), .b(b), .d(d), .out_7(Code_3_out_7));
  Flags__AND__OR__XOR__LOAD AND__OR__XOR__LOAD (.Flags(Flags), .Rd_out(Rd_out), .Flags_2(AND__OR__XOR__LOAD_flags_2));
  Multiplexer #(.width(5)) multiplexer_1 (
    .in0(Code_3_out_7), .in1(flags_inc_dec_1_flags_2), .out(multiplexer_1_out), .sel(a[3]));  // open: en
  Flags__INC__DEC flags_inc_dec_1 (
    .Flags(Flags), .Rd_out(Rd_out), .INC_out(inc_out), .Dec_out(dec_out), .Ra(Ra), .Rb(Rb), .a2(a[2]),
    .Flags_2(flags_inc_dec_1_flags_2));
  Multiply Multiplier (.Ra(Ra), .Rb(Rb), .Flags_out(Multiplier_flags_out), .Flags_in(Flags));  // open: Rd
  Multiplexer #(.select(4), .width(5)) multiplexer_2 (
    .in0(Flags), .in1(Flags), .in2(AND__OR__XOR__LOAD_flags_2), .in3(multiplexer_1_out),
    .in4(AND__OR__XOR__LOAD_flags_2), .in5(AND__OR__XOR__LOAD_flags_2), .in6(Flags), .in7(Flags),
    .in8(AND__OR__XOR__LOAD_flags_2), .in9(AND__OR__XOR__LOAD_flags_2), .in10(ADD_SUB_flags_2),
    .in11(ADD_SUB_flags_2), .in12(Multiplier_flags_out), .in13(AND__OR__XOR__LOAD_flags_2), .in14(Flags),
    .in15(Flags), .out(Flags_2), .sel(Opcode));  // open: en

  // Other names for the same wires on the sheet: b_out = Borrow_out; c_out = Carry_out; Flags_in[4:0] = Flags

  // Notes on the sheet:
  //   This module contains all the logic for flag changes
  //   The mux is used to decide the approriate combinational circuit for current operation
endmodule

module ADD_d_b_b (
  input  [15:0] Rb,
  output overflow
);

  wire [15:0] adder_1_out;

  Adder #(.width(16)) adder_1 (.a(Rb), .b(Rb), .out(adder_1_out));  // open: cin, cout
  xor xor_1 (overflow, adder_1_out[15], Rb[15]);
endmodule

module Flags__INC__DEC (
  input  [4:0] Flags,
  input  [15:0] Rd_out,
  input  INC_out,
  input  Dec_out,
  input  [15:0] Ra,
  input  a2,
  input  [15:0] Rb,
  output [4:0] Flags_2
);

  wire and_1_out, and_2_out, and_3_out, and_4_out, or_1_out, or_2_out;

  Comparator #(.width(16)) comparator_1 (.a(Rd_out), .b({16{1'b0}}), .eq(Flags_2[1]));  // open: gt, lt
  and and_1 (and_1_out, Rd_out[15], ~Ra[15], ~Rb[15]);  // AND_Gate
  and and_2 (and_2_out, ~Rd_out[15], Ra[15], Rb[15]);  // AND_Gate
  and and_3 (and_3_out, Rd_out[15], ~Ra[15], Rb[15]);  // AND_Gate
  and and_4 (and_4_out, ~Rd_out[15], Ra[15], ~Rb[15]);  // AND_Gate
  or or_1 (or_1_out, and_1_out, and_2_out);
  or or_2 (or_2_out, and_3_out, and_4_out);
  Multiplexer multiplexer_1 (.in0(or_1_out), .in1(or_2_out), .out(Flags_2[2]), .sel(a2));  // open: en
  Multiplexer multiplexer_2 (.in0(INC_out), .in1(Dec_out), .out(Flags_2[3]), .sel(a2));  // open: en

  assign {Flags_2[4], Flags_2[0]} = {Flags[4], Rd_out[15]};

  // Notes on the sheet:
  //   Sign
  //   Check if op is inc/dec
  //   Carry Block
  //   Zero
endmodule

module Load_Store (
  input  [15:0] Store_Data,
  input  Clock,
  input  [3:0] Opcode,
  input  [4:0] o,
  input  [15:0] Rb,
  output [15:0] Load_store_data
);

  wire comparator_1_eq, not_1_out;
  wire [15:0] Address, bit_extender_1_out;

  Comparator #(.width(3)) comparator_1 (.a(Opcode[3:1]), .b(3'b011), .eq(comparator_1_eq));  // open: gt, lt
  assign bit_extender_1_out = {{11{1'b0}}, o};  // Bit_Extender bit_extender_1
  assign Load_store_data = comparator_1_eq ? Store_Data : 16'bz;  // Controlled_Buffer controlled_buffer_1
  not not_1 (not_1_out, comparator_1_eq);
  Adder #(.width(16)) adder_1 (.a(bit_extender_1_out), .b(Rb), .out(Address));  // open: cin, cout
  RAM #(.addrWidth(16), .dataWidth(16)) ram_1 (
    .addr(Address), .data(Load_store_data), .clk(Clock), .ld(not_1_out));  // open: sel, clr

  // Notes on the sheet:
  //   Store doesn't affect Rd/flags whereas Load does
endmodule

module Multiply (
  input  [15:0] Ra,
  input  [15:0] Rb,
  input  [4:0] Flags_in,
  output [15:0] Rd,
  output [4:0] Flags_out
);

  wire and_1_out, comparator_1_eq, comparator_1_gt, comparator_3_eq;
  wire [31:0] bit_extender_1_out, bit_extender_2_out, bit_extender_3_out, bit_extender_4_out,
       bit_extender_5_out, multiplier_1_out, multiplier_2_out;

  assign bit_extender_1_out = {{16{Ra[15]}}, Ra};  // Bit_Extender bit_extender_1
  assign bit_extender_2_out = {{16{Rb[15]}}, Rb};  // Bit_Extender bit_extender_2
  assign bit_extender_3_out = {{16{1'b0}}, Ra};  // Bit_Extender bit_extender_3
  assign bit_extender_4_out = {{16{1'b0}}, Rb};  // Bit_Extender bit_extender_4
  and and_1 (and_1_out, Flags_in[0], ~Flags_in[1], ~Flags_in[2], ~Flags_in[3], ~Flags_in[4]);  // AND_Gate
  Multiplier #(.width(32)) multiplier_1 (
    .a(bit_extender_1_out), .b(bit_extender_2_out), .out(multiplier_1_out));  // open: cin, cout
  Multiplier #(.width(32)) multiplier_2 (
    .a(bit_extender_3_out), .b(bit_extender_4_out), .out(multiplier_2_out));  // open: cin, cout
  Comparator #(.width(32), .mode("unsigned")) comparator_1 (
    .a(multiplier_2_out), .b(32'h10000), .gt(comparator_1_gt), .eq(comparator_1_eq));  // open: lt
  and and_2 (Flags_out[0], multiplier_1_out[15], 1'b1);
  Comparator #(.width(32)) comparator_2 (.a(multiplier_1_out), .b({32{1'b0}}), .eq(Flags_out[1]));  // open: gt, lt
  or or_1 (Flags_out[3], comparator_1_gt, comparator_1_eq);
  assign bit_extender_5_out = {{16{multiplier_1_out[15]}}, multiplier_1_out[15:0]};  // Bit_Extender bit_extender_5
  Comparator #(.width(32)) comparator_3 (
    .a(bit_extender_5_out), .b(multiplier_1_out), .eq(comparator_3_eq));  // open: gt, lt
  not not_1 (Flags_out[2], comparator_3_eq);
  Multiplexer #(.width(16)) multiplexer_1 (
    .in0(multiplier_1_out[15:0]), .in1(multiplier_1_out[31:16]), .out(Rd), .sel(and_1_out));  // open: en

  assign Flags_out[4] = Flags_in[4];

  // Notes on the sheet:
  //   Carry is on if multiplying the zero-extended versions of Ra and Rb gives something >= 2^16
  //   Compare the sign-extended version of the lower 16 bits and the product itself will produce the OPPOSITE of final overflow
  //   For multiply, I extend the 2 inputs to 32 bits, multiply them using built-in multiplier. Rd will be the higher 16 bits of this product iff only sign flag is true and lower 16 bits otherwise
endmodule

module main (
  output [3:0] opcode,
  output [3:0] d__Write_Reg,
  output [3:0] a__Read_Reg__1,
  output [15:0] Rd,
  output [3:0] b__Read_Reg__2,
  output [15:0] Load_Store_val
);

  wire Branch_Module_relative, Call_return, clock_1_out, comparator_1_lt, comparator_2_eq, not_1_out, PC_Load;
  wire [3:0] d_or_b, Register_File_r1_2, Register_File_r2, Register_File_r2_2, Register_File_r2_3,
       Register_File_r2_4, Register_File_r3, Register_File_r3_2, Register_File_r3_3, Register_File_r3_4;
  wire [4:0] ALSU_flags, Flag;
  wire [15:0] adder_1_out, adder_2_out, offset, PC_Data, PC_q, Ra, Rb, Rd_or_PC_1, Rd_t, Register_File_r1;

  Clock clock_1 (.out(clock_1_out));
  Branch_Conditions Branch_Module (
    .Flags(Flag), .Instruction({opcode, d__Write_Reg, a__Read_Reg__1, b__Read_Reg__2}),
    .Relative(Branch_Module_relative), .Branch(PC_Load));
  Counter #(.width(16), .max('hffff), .ongoal("stay")) PC (
    .load(PC_Load), .D(PC_Data), .count(not_1_out), .Q(PC_q), .clk(clock_1_out));  // open: carry, clr
  not not_1 (not_1_out, PC_Load);
  Adder #(.width(16)) adder_1 (.a(offset), .b(PC_q), .out(adder_1_out));  // open: cin, cout
  Multiplexer #(.width(16), .enable("false")) multiplexer_1 (
    .in0(Rb), .in1(adder_1_out), .out(PC_Data), .sel(Branch_Module_relative));
  ROM #(.addrWidth(16), .dataWidth(16)) rom_1 (
    .addr(PC_q), .data({opcode, d__Write_Reg, a__Read_Reg__1, b__Read_Reg__2}));  // open: sel
  Comparator #(.width(4), .mode("unsigned")) comparator_1 (
    .a(d__Write_Reg), .b(4'b0010), .lt(comparator_1_lt));  // open: gt, eq
  Comparator #(.width(4), .mode("unsigned")) comparator_2 (
    .a(4'b0010), .b(opcode), .eq(comparator_2_eq));  // open: gt, lt
  Adder #(.width(16)) adder_2 (.a(PC_q), .b(16'h1), .out(adder_2_out));  // open: cin, cout
  and u_Call_return (Call_return, comparator_1_lt, comparator_2_eq);
  assign offset = {{8{a__Read_Reg__1[3]}}, {a__Read_Reg__1, b__Read_Reg__2}};  // Bit_Extender bit_extender_1
  Multiplexer #(.width(16)) multiplexer_2 (
    .in0(Rd), .in1(adder_2_out), .out(Rd_or_PC_1), .sel(Call_return));  // open: en
  Load_Store Load_Store (
    .Store_Data(Rd_t), .Clock(clock_1_out), .Opcode(opcode), .o({opcode[0], a__Read_Reg__1}), .Rb(Rb),
    .Load_store_data(Load_Store_val));
  Multiplexer #(.width(4)) multiplexer_3 (
    .in0(d__Write_Reg), .in1(b__Read_Reg__2), .out(d_or_b), .sel(Call_return));  // open: en
  Register_Bank Register_File (
    .d(d_or_b), .Call_return(Call_return), .Rd(Rd_or_PC_1), .a(a__Read_Reg__1), .b(b__Read_Reg__2),
    .Clock(clock_1_out), .R1({Register_File_r1[15:8], Register_File_r1_2, Register_File_r1[3:0]}),
    .R2({Register_File_r2_4, Register_File_r2_3, Register_File_r2_2, Register_File_r2}),
    .R3({Register_File_r3_4, Register_File_r3_3, Register_File_r3_2, Register_File_r3}), .Ra(Ra), .Rb(Rb),
    .Rd_2(Rd_t));
  Hex_Digit_Display hex_digit_display_1 (.value(Register_File_r1[11:8]));  // open: dp
  Hex_Digit_Display hex_digit_display_2 (.value(Register_File_r1[15:12]));  // open: dp
  ALSU ALSU (
    .Flags_in(Flag), .Ra(Ra), .Rb(Rb), .a(a__Read_Reg__1), .b(b__Read_Reg__2), .d(d__Write_Reg), .Rd(Rd_t),
    .Load_Store_Value(Load_Store_val), .Opcode(opcode), .Flags(ALSU_flags), .Rd_2(Rd));
  Hex_Digit_Display hex_digit_display_3 (.value(Register_File_r1_2));  // open: dp
  Hex_Digit_Display hex_digit_display_4 (.value(Register_File_r1[3:0]));  // open: dp
  Flag_Bank Flag_Bank (.Flags(ALSU_flags), .Clk(clock_1_out), .Flags_Out(Flag));
  Hex_Digit_Display hex_digit_display_5 (.value(Register_File_r2_4));  // open: dp
  Hex_Digit_Display hex_digit_display_6 (.value(Register_File_r3_4));  // open: dp
  DotMatrix #(.inputtype("row"), .matrixrows(1), .dotshape("circle")) dotmatrix_1 (.row0(Flag));
  Hex_Digit_Display hex_digit_display_7 (.value(Register_File_r2_3));  // open: dp
  Hex_Digit_Display hex_digit_display_8 (.value(Register_File_r3_3));  // open: dp
  Hex_Digit_Display hex_digit_display_9 (.value(Register_File_r2_2));  // open: dp
  Hex_Digit_Display hex_digit_display_10 (.value(Register_File_r2));  // open: dp
  Hex_Digit_Display hex_digit_display_11 (.value(Register_File_r3_2));  // open: dp
  Hex_Digit_Display hex_digit_display_12 (.value(Register_File_r3));  // open: dp

  // Other names for the same wires on the sheet: a[3:0] = a__Read_Reg__1;
  //   Instructions[15:0] = {opcode, d__Write_Reg, a__Read_Reg__1, b__Read_Reg__2}; b[3:0] = b__Read_Reg__2;
  //   d[3:0] = d__Write_Reg

  // Notes on the sheet:
  //   Branch?
  //   PC Load indicates whether to branch or not
  //   Relative?
  //   ALSU constructed by Ha Phan
  //   Note: Counter is triggered on falling edge 
  //   ROM
  //   Flags: F4F3F2F1F0, F4 is carry block, F0 is sign
  //   contents of rom_1 (hex, n*v repeats v):
  //   3160 e105 f100 e20a f200 9312
  //   PC becomes current PC + offset if we branch relative and Rb otherwise
  //   to decide if we're changing register d or b in the register file
  //   write Rd_in to register d when no call/return
  //   write PC + 1 to register b when call/return
  //   There's a RAM inside Load/Store module
  //   R1
  //   R2
  //   R3
  //   Flags
endmodule

module Branch_Conditions (
  input  [4:0] Flags,
  input  [15:0] Instruction,
  output Relative,
  output Branch
);

  wire Branch_code, c_prime_V_z, Call_return_out, comparator_1_eq, comparator_3_lt, comparator_4_eq,
       multiplexer_1_out, multiplexer_3_out, not_1_out, not_2_out, not_3_out, not_4_out, not_5_out,
       not_6_out, not_7_out, Relative_code, s_xor_v, s_xor_v__V_z;

  xor xor_1 (s_xor_v, Flags[0], Flags[2]);
  or or_1 (s_xor_v__V_z, s_xor_v, Flags[1]);
  or or_2 (c_prime_V_z, ~Flags[3], Flags[1]);  // OR_Gate
  Comparator #(.width(4), .mode("unsigned")) comparator_1 (
    .a(Instruction[15:12]), .b(4'b0001), .eq(comparator_1_eq));  // open: gt, lt
  Comparator #(.width(4), .mode("unsigned")) comparator_2 (
    .a(Instruction[15:12]), .b(4'b0000), .eq(Relative_code));  // open: gt, lt
  not not_1 (not_1_out, s_xor_v);
  not not_2 (not_2_out, s_xor_v__V_z);
  not not_3 (not_3_out, c_prime_V_z);
  not not_4 (not_4_out, Flags[1]);
  not not_5 (not_5_out, Flags[3]);
  not not_6 (not_6_out, Flags[0]);
  not not_7 (not_7_out, Flags[2]);
  or or_3 (Branch_code, comparator_1_eq, Relative_code);
  Multiplexer #(.select(4)) multiplexer_1 (
    .in0(1'b1), .in1(1'b0), .in2(s_xor_v), .in3(not_1_out), .in4(s_xor_v__V_z), .in5(not_2_out),
    .in6(c_prime_V_z), .in7(not_3_out), .in8(Flags[1]), .in9(not_4_out), .in10(Flags[3]), .in11(not_5_out),
    .in12(Flags[0]), .in13(not_6_out), .in14(Flags[2]), .in15(not_7_out), .out(multiplexer_1_out),
    .sel(Instruction[11:8]));  // open: en
  Comparator #(.width(4), .mode("unsigned")) comparator_3 (
    .a(Instruction[11:8]), .b(4'b0010), .lt(comparator_3_lt));  // open: gt, eq
  Comparator #(.width(4), .mode("unsigned")) comparator_4 (
    .a(4'b0010), .b(Instruction[15:12]), .eq(comparator_4_eq));  // open: gt, lt
  Multiplexer multiplexer_2 (.in0(1'b0), .in1(multiplexer_1_out), .out(Relative), .sel(Relative_code));  // open: en
  Multiplexer multiplexer_3 (
    .in0(1'b0), .in1(multiplexer_1_out), .out(multiplexer_3_out), .sel(Branch_code));  // open: en
  and Call_return (Call_return_out, comparator_3_lt, comparator_4_eq);
  or or_4 (Branch, multiplexer_3_out, Call_return_out);

  // Other names for the same wires on the sheet: s = Flags[0]; z = Flags[1]; v = Flags[2]; c = Flags[3];
  //   b[3:0] = Instruction[3:0]; b7_4[3:0] = Instruction[7:4]; b11_8[3:0] = Instruction[11:8];
  //   b15_12[3:0] = Instruction[15:12]

  // Notes on the sheet:
  //   Check for branch if b15:12 is either 0000 or 0001
  //   Check for relative branch if b15:12 is 0000
  //   If there's a need to check for branch, do so here
  //   by checking if branching conditions are satisfied
endmodule
